# Fritzing sketch Fritzing4CodeWriter (saved by Fritzing 0.9.6b)
breadboards: 1

parts:
  Part1 = Arduino Uno (Rev3)
  R1 = Resistor [tolerance=±5% power=0.25 resistance=220 package=THT]
  S1 = Square Pushbutton

nets:
  N1: Part1.GND, S1.leg0
  N2: Part1.D3_PWM, R1.Pin_1, S1.leg1
  N3: Part1.3V3, R1.Pin_0
