# Fritzing sketch solenoid (saved by Fritzing 0.9.6b)
breadboards: 1

parts:
  Q1 = MOSFET-NCHANNEL [package=to220v]
  Part1 = Arduino Uno (Rev3)
  R1 = Resistor [tolerance=±5% power=0.25 resistance=220 package=THT]
  D1 = Rectifier Diode [part_number=1N4001 package="300 mil [THT]"]
  VCC1 = Battery block 9V
  L1 = Solenoid

nets:
  N1: Q1.G, Part1.D3_PWM, R1.Pin_0
  N2: Q1.D, D1.cathode, D1.anode, L1.pin1
  N3: Q1.S, Part1.GND, R1.Pin_1, VCC1.-
