# Fritzing sketch LCD_with_mic (saved by Fritzing 0.9.6b)

parts:
  Part1 = Breakout Board for Electret Microphone
  LCD2 = LCD screen
  LCM1602_IIC3 = LCM1602 IIC [part_number="LCM1602 IIC" chip_label="LCM1602 IIC" package="DIP (Dual Inline) [THT]"]
  Part2 = Arduino Uno (Rev3)

nets:
  VCC: Part1.VCC, Part2.3V3
  GND: Part1.GND, LCM1602_IIC3.GND, Part2.GND
  N1: Part1.AUD, Part2.A0
  VSS: LCD2.VSS, LCM1602_IIC3.VSS
  VDD: LCD2.VDD, LCM1602_IIC3.VDD
  N2: LCD2.V0, LCM1602_IIC3.V0
  N3: LCD2.RS, LCM1602_IIC3.RS
  N4: LCD2.R/W, LCM1602_IIC3.RW
  N5: LCD2.E, LCM1602_IIC3.E
  N6: LCD2.DB0, LCM1602_IIC3.D0
  N7: LCD2.DB1, LCM1602_IIC3.D1
  N8: LCD2.DB2, LCM1602_IIC3.D2
  N9: LCD2.DB3, LCM1602_IIC3.D3
  N10: LCD2.DB4, LCM1602_IIC3.D4
  N11: LCD2.DB5, LCM1602_IIC3.D5
  N12: LCD2.DB6, LCM1602_IIC3.D6
  N13: LCD2.DB7, LCM1602_IIC3.D7
  N14: LCD2.LED+, LCM1602_IIC3.A
  N15: LCD2.LED-, LCM1602_IIC3.K
  VCC_2: LCM1602_IIC3.VCC, Part2.5V
  N16: LCM1602_IIC3.SDA, Part2.A4/SDA
  N17: LCM1602_IIC3.SCL, Part2.A5/SCL
  N18: LCM1602_IIC3.LED_A, LCM1602_IIC3.LED_B

custom parts:
  LCM1602 IIC: I2C-Module to use a 1602 or 2004 LCD on with the wire.h libory Serial LCD Modul
